// Logisim project traffic-light-system.circ as structural Verilog: 6 circuits, main circuit main
module main (
  input  Signal,
  input  Zero,
  input  [2:0] Mode
);

  wire clock_1_out, diff_detector_1_output, G1, G2, G3, G4, GL1, GL2, GL3, GL4, P1, P2, P3, P4, PG1, PG2,
       PG3, PG4, PR1, PR2, PR3, PR4, R1, R2, R3, R4, Y1, Y2, Y3, Y4;
  wire [2:0] E, N, S, W;
  wire [3:0] n4_bit_counter_1_d0;

  Clock clock_1 (.out(clock_1_out));
  traffic_signal traffic_signal_1 (
    .in_1(E), .out_3(R2), .out_4(Y2), .out_6(G2), .out_8(PG2), .out_7(PR2), .in_2(P2), .out_5(GL2));
  _4_bit_counter u_4_bit_counter_1 (
    .Power(Signal), .Zero(Zero), .d0(n4_bit_counter_1_d0[0]), .d1(n4_bit_counter_1_d0[1]),
    .d2(n4_bit_counter_1_d0[2]), .d3(n4_bit_counter_1_d0[3]), .Clock(clock_1_out),
    .in_4(diff_detector_1_output));
  diff_detector diff_detector_1 (.Mode(Mode), .Output(diff_detector_1_output), .Clock(clock_1_out));
  traffic_signal traffic_signal_2 (
    .in_1(N), .out_3(R3), .out_4(Y3), .out_6(G3), .out_8(PG3), .out_7(PR3), .in_2(P3), .out_5(GL3));
  Hex_Digit_Display hex_digit_display_1 (.value(n4_bit_counter_1_d0));  // open: dp
  traffic_signal traffic_signal_3 (
    .in_1(W), .out_3(R4), .out_4(Y4), .out_6(G4), .out_8(PG4), .out_7(PR4), .in_2(P4), .out_5(GL4));
  traffic_signal traffic_signal_4 (
    .in_1(S), .out_3(R1), .out_4(Y1), .out_6(G1), .out_8(PG1), .out_7(PR1), .in_2(P1), .out_5(GL1));
  // controller controller_1: pin names not known; wires that end beside it: n4_bit_counter_1_d0, Mode, P4, P3, P2, P1, S, E, N, W
  LED led_1 (.in(R4));
  LED led_2 (.in(Y4));
  LED led_3 (.in(GL4));
  LED led_4 (.in(G4));
  LED led_5 (.in(PR4));
  LED led_6 (.in(PG4));
  LED led_7 (.in(R3));
  LED led_8 (.in(G3));
  LED led_9 (.in(Y3));
  LED led_10 (.in(GL3));
  LED led_11 (.in(PR3));
  LED led_12 (.in(PG3));
  LED led_13 (.in(PR1));
  LED led_14 (.in(PG1));
  LED led_15 (.in(GL1));
  LED led_16 (.in(G1));
  LED led_17 (.in(Y1));
  LED led_18 (.in(R1));
  LED led_19 (.in(PR2));
  LED led_20 (.in(PG2));
  LED led_21 (.in(G2));
  LED led_22 (.in(GL2));
  LED led_23 (.in(Y2));
  LED led_24 (.in(R2));

  // Notes on the sheet:
  //   Clock
  //   NORTH
  //   EAST
  //   Control Circuit
  //   System v1.0.0
  //   Released on May 28, 2021
  //   Copyright (c) 2021 Capella87
  //   github.com/Capella87/traffic-light-system
  //   WEST
  //   SOUTH
  //   State
  //   WEST
  //   Traffic Light System in crossroad
  //   NORTH
  //   SOUTH
  //   EAST
endmodule

module _4_bit_counter (
  input  Power,
  input  Zero,
  input  Clock,
  input  in_4,
  output d0,
  output d1,
  output d2,
  output d3
);

  wire and_1_out, and_2_out, not_1_out, or_1_out;

  or or_1 (or_1_out, Zero, in_4);
  not not_1 (not_1_out, Clock);
  J_K_Flip_Flop j_k_ff_1 (.J(Power), .clk(not_1_out), .K(Power), .Q(d0), .reset(or_1_out));  // open: Qn, preset, en
  and and_1 (and_1_out, d0, d1);
  J_K_Flip_Flop j_k_ff_2 (.J(d0), .clk(not_1_out), .K(d0), .Q(d1), .en(Power), .reset(or_1_out));  // open: Qn, preset
  J_K_Flip_Flop j_k_ff_3 (
    .J(and_1_out), .clk(not_1_out), .K(and_1_out), .Q(d2), .en(Power), .reset(or_1_out));  // open: Qn, preset
  and and_2 (and_2_out, d0, d1, d2);
  J_K_Flip_Flop j_k_ff_4 (
    .J(and_2_out), .clk(not_1_out), .K(and_2_out), .Q(d3), .en(Power), .reset(or_1_out));  // open: Qn, preset

  // Notes on the sheet:
  //   Diff
endmodule

module controller (
  input  [3:0] Counter_input,
  input  [2:0] Mode,
  output [1:0] South,
  output [1:0] East,
  output [1:0] North,
  output [1:0] West
);

  wire not_1_out, not_2_out, not_3_out, not_4_out, not_5_out, not_6_out, not_7_out, or_1_out;
  wire [3:0] demultiplexer_1_out0, demultiplexer_1_out1, demultiplexer_1_out2;

  Demultiplexer #(.select(3), .width(4)) demultiplexer_1 (
    .out0(demultiplexer_1_out0), .out1(demultiplexer_1_out1), .out2(demultiplexer_1_out2),
    .in(Counter_input), .sel(Mode));  // open: out3, out4, out5, out6, out7, en
  not not_1 (not_1_out, demultiplexer_1_out0[3]);
  not not_2 (not_2_out, demultiplexer_1_out0[2]);
  not not_3 (not_3_out, demultiplexer_1_out0[1]);
  not not_4 (not_4_out, demultiplexer_1_out0[0]);
  not not_5 (not_5_out, demultiplexer_1_out0[3]);
  not not_6 (not_6_out, demultiplexer_1_out0[2]);
  not not_7 (not_7_out, demultiplexer_1_out0[2]);
  or or_1 (or_1_out, not_3_out, not_4_out);
  and and_1 (South[0], demultiplexer_1_out0[0], demultiplexer_1_out0[1], not_1_out, not_2_out);
  and and_2 (South[1], not_1_out, not_2_out, or_1_out);
  and and_3 (East[0], not_5_out, demultiplexer_1_out0[2], demultiplexer_1_out0[1], demultiplexer_1_out0[0]);
  and and_4 (East[1], not_5_out, demultiplexer_1_out0[2], or_1_out);
  and and_5 (North[0], demultiplexer_1_out0[3], not_6_out, demultiplexer_1_out0[1], demultiplexer_1_out0[0]);
  and and_6 (North[1], demultiplexer_1_out0[3], not_7_out, or_1_out);
  and and_7 (West[0], demultiplexer_1_out0[3], demultiplexer_1_out0[2], demultiplexer_1_out0[1], demultiplexer_1_out0[0]);
  and and_8 (West[1], demultiplexer_1_out0[3], demultiplexer_1_out0[2], or_1_out);

  // Notes on the sheet:
  //   Simultaneous-Straight-Left
  //   Straight-and-Left
  //   Left-and-Straight
endmodule

module traffic_signal (
  input  [2:0] in_1,
  input  in_2,
  output out_3,
  output out_4,
  output out_5,
  output out_6,
  output out_7,
  output out_8
);

  wire and_2_out, and_3_out, and_4_out, and_5_out, not_1_out, not_2_out, not_3_out, not_4_out, not_5_out,
       not_6_out, or_1_out, or_4_out;

  not not_1 (not_1_out, in_1[0]);
  not not_2 (not_2_out, in_1[1]);
  not not_3 (not_3_out, in_1[0]);
  not not_4 (not_4_out, in_1[2]);
  not not_5 (not_5_out, in_1[1]);
  not not_6 (not_6_out, in_1[2]);
  not not_7 (out_7, in_2);
  and and_1 (out_3, not_1_out, or_1_out);
  or or_1 (or_1_out, not_2_out, in_1[2]);
  and and_2 (and_2_out, not_3_out, in_1[1]);
  or or_2 (out_4, and_2_out, and_3_out);
  and and_3 (and_3_out, in_1[2], in_1[0]);
  and and_4 (and_4_out, in_1[0], in_1[1], not_4_out);
  or or_3 (out_5, and_4_out, and_5_out);
  and and_5 (and_5_out, not_5_out, in_1[2]);
  and and_6 (out_6, in_1[0], or_4_out);
  or or_4 (or_4_out, in_1[1], not_6_out);
  LED led_1 (.in(out_3));
  LED led_2 (.in(out_4));
  LED led_3 (.in(out_5));
  LED led_4 (.in(out_6));
  LED led_5 (.in(out_7));
  LED led_6 (.in(in_2));

  assign out_8 = in_2;

  // Other names for the same wires on the sheet: G = out_6; GL = out_5; PG = in_2; PR = out_7; R = out_3; Y = out_4

  // Notes on the sheet:
  //   Car traffic light
  //   Pedestrian Light
endmodule

module diff_detector (
  input  [2:0] Mode,
  input  Clock,
  output Output
);

  wire comparator_1_output, comparator_2_output, comparator_3_output, d_ff_1_q, d_ff_2_q, d_ff_3_q;

  D_Flip_Flop d_ff_1 (.clk(Clock), .D(Mode[0]), .Q(d_ff_1_q));  // open: Qn, preset, en, reset
  D_Flip_Flop d_ff_2 (.clk(Clock), .D(Mode[1]), .Q(d_ff_2_q));  // open: Qn, preset, en, reset
  D_Flip_Flop d_ff_3 (.clk(Clock), .D(Mode[2]), .Q(d_ff_3_q));  // open: Qn, preset, en, reset
  comparator comparator_1 (.d1(d_ff_1_q), .d2(Mode[0]), .\output (comparator_1_output));
  comparator comparator_2 (.d1(d_ff_2_q), .d2(Mode[1]), .\output (comparator_2_output));
  comparator comparator_3 (.d1(d_ff_3_q), .d2(Mode[2]), .\output (comparator_3_output));
  nand nand_1 (Output, comparator_1_output, comparator_2_output, comparator_3_output);
endmodule

module comparator (
  input  d1,
  input  d2,
  output \output 
);

  xnor xnor_1 (\output , d1, d2);
endmodule
